# Fritzing sketch mécanisme air (saved by Fritzing 0.9.3b)
breadboards: 1

parts:
  Composant1 = Arduino Nano (Rev3.0)
  U1 = RELAY-SOLIDSTATE [package=relay-s108t02]
  U2 = RELAY-SOLIDSTATE [package=relay-s108t02]
  LED1 = smd LED [color="Red (633nm)" package="0603 [SMD]"]
  LED2 = DUO LED RG [package="5 mm [THT]"]  # not connected
  R1 = Resistor [tolerance=±5% resistance=220 package="0402 [SMD]"]  # not connected
  R2 = Resistor [tolerance=±5% resistance=220 package="0402 [SMD]"]  # not connected
  Btn1 = Adafruit Push-button Power Switch Breakout [package=THT]
  R3 = PHOTOCELL [package=photocell]
  R4 = PHOTOCELL [package=photocell]
  R5 = PHOTOCELL [package=photocell]
  R6 = PHOTOCELL [package=photocell]
  R7 = PHOTOCELL [package=photocell]
  R8 = PHOTOCELL [package=photocell]
  R9 = PHOTOCELL [package=photocell]

nets:
  GND: Composant1.GND, Composant1.D2, U2.-, Btn1.GND, R3.P$2, R4.P$2, R5.P$2, R6.P$2, R7.P$2, R8.P$2, R9.P$2
  N1: Composant1.D5, Btn1.OUT
  N2: Composant1.D8, U2.+
  N3: Composant1.D9, Composant1.D10, U1.+
  N4: Composant1.A7, R6.P$1
  N5: Composant1.A6, R8.P$1
  N6: Composant1.A5, R5.P$1
  N7: Composant1.A4, R3.P$1
  N8: Composant1.A3, R4.P$1
  N9: Composant1.A2, R7.P$1
  N10: Composant1.A1, R9.P$1
  N11: LED1.cathode, LED1.anode
